# Fritzing sketch room_light_final (saved by Fritzing 0.9.6)

parts:
  Arduino_MKR_WiFi_1010_(VIN_from_5_V_rail) = Arduino MKR WIFI 1010
  Barrel_jack_(5_V_4_A_supply) = Power Jack [package=power_jack_slot]
  POWER_IN_screw_terminal = Camdenboss CTB0158-2 [package=THT]
  74AHCT125_level_shifter_(74ACT125_stand-in_same_pinout) = 74ACT125D [package=so014]
  0_1_uF_decoupling = Ceramic Capacitor [capacitance=100nF package="200 mil [THT, multilayer]"]
  470_ohm_data_resistor = Resistor [resistance=470Ω package=THT]
  1000_uF_at_the_strip = Electrolytic Capacitor [capacitance=1000µF voltage=10V package="200 mil [THT, electrolytic]"]
  JST_SM_3-pin_pigtail_(to_strip) = JST-B3P-VH [package=THT]
  Adafruit_4689_NeoPixel_RGBW_neon_strip_(stand-in) = WS2815 RGB LED strip

nets:
  GND: Arduino_MKR_WiFi_1010_(VIN_from_5_V_rail).GND, POWER_IN_screw_terminal.terminal_2, 74AHCT125_level_shifter_(74ACT125_stand-in_same_pinout).A0, 74AHCT125_level_shifter_(74ACT125_stand-in_same_pinout).A1, 74AHCT125_level_shifter_(74ACT125_stand-in_same_pinout).B1, 74AHCT125_level_shifter_(74ACT125_stand-in_same_pinout).GND, 74AHCT125_level_shifter_(74ACT125_stand-in_same_pinout).B3, 74AHCT125_level_shifter_(74ACT125_stand-in_same_pinout).A3, 74AHCT125_level_shifter_(74ACT125_stand-in_same_pinout).B2, 74AHCT125_level_shifter_(74ACT125_stand-in_same_pinout).A2, 0_1_uF_decoupling.1, 1000_uF_at_the_strip.-, JST_SM_3-pin_pigtail_(to_strip).pin3, Adafruit_4689_NeoPixel_RGBW_neon_strip_(stand-in).GND
  N1: Arduino_MKR_WiFi_1010_(VIN_from_5_V_rail).D6, 74AHCT125_level_shifter_(74ACT125_stand-in_same_pinout).B0
  VCC: Arduino_MKR_WiFi_1010_(VIN_from_5_V_rail).VIN, POWER_IN_screw_terminal.terminal_1, 74AHCT125_level_shifter_(74ACT125_stand-in_same_pinout).VCC, 0_1_uF_decoupling.0, 1000_uF_at_the_strip.+, JST_SM_3-pin_pigtail_(to_strip).pin2, Adafruit_4689_NeoPixel_RGBW_neon_strip_(stand-in).VCC
  N2: Barrel_jack_(5_V_4_A_supply).GND, POWER_IN_screw_terminal.pin2
  N3: Barrel_jack_(5_V_4_A_supply).PWR, POWER_IN_screw_terminal.pin1
  N4: 74AHCT125_level_shifter_(74ACT125_stand-in_same_pinout).O0, 470_ohm_data_resistor.Pin_0
  N5: 470_ohm_data_resistor.Pin_1, JST_SM_3-pin_pigtail_(to_strip).pin1, Adafruit_4689_NeoPixel_RGBW_neon_strip_(stand-in).DIN

custom parts:
  Arduino MKR WIFI 1010: The MKR WIFI 1010 is a significant improvement on the MKR 1000 WIFI. It's equipped with an ESP32 module made by U-BLOX. This board aims to speed up and simplify the prototyping of WiFi based IoT applications thanks to the flexibility of the ESP32 module and its low power consumption. The board is composed of three main blocks: SAMD21 Cortex-M0+ 32bit Low Power ARM MCU; U-BLOX NINA-W10 Series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
